# Fritzing sketch ArduinoLidarLiteV3Diagram (saved by Fritzing 0.9.3b)
breadboards: 1

parts:
  Part1 = Arduino Due (Rev2b)
  J1 = Basic Servo
  VCC1 = 4 x AAA Battery Mount
  J2 = Basic Servo
  C1 = Electrolytic Capacitor [capacitance=4.7mF package="0605 [SMD, electrolytic]"]
  C3 = Electrolytic Capacitor [capacitance=1mF package="0605 [SMD, electrolytic]"]
  C4 = Electrolytic Capacitor [capacitance=1mF package="0605 [SMD, electrolytic]"]
  R1 = Resistor [tolerance=±5% resistance=4.7k package="2512 [SMD]"]
  R2 = Resistor [tolerance=±5% resistance=4.7k package="2512 [SMD]"]
  Part2 = LIDAR-Lite

nets:
  N1: Part1.D20/SDA3, R2.Pin_1, Part2.SDA
  N2: Part1.D21/SCL3, R1.Pin_1, Part2.SCL
  5V: Part1.5V, C1.+, C3.+, C4.+, R1.Pin_0, R2.Pin_0, Part2.5V
  GND: Part1.GND, J1.gnd, VCC1.-, J2.gnd, C1.-, C3.-, C4.-, Part2.GND
  N3: Part1.D9_PWM, J2.pulse
  N4: Part1.D10_PWM/SS0, J1.pulse
  VCC: J1.vcc, VCC1.+, J2.vcc

custom parts:
  LIDAR-Lite: PulsedLight LIDAR-Lite Sensor
